# Fritzing sketch Memoria (saved by Fritzing 0.9.3b)
breadboards: 1

parts:
  Εξάρτημα2 = Arduino Nano (Rev3.0)
  Part1 = Adafruit MAX9814 Electret Microphone Amplifier [part_number="Adafruit #1713"]
  SD_card_module1 = SD Card Module
  LED2 = LED - 5mm [color="Red (633nm)" package="5 mm [THT]"]
  R2 = Resistor [tolerance=±5% resistance=220 package=THT]
  S3 = Toggle Switch [package=THT]
  M1 = NEO-6M GPS Module [part_number=GY-GPS6MV2]
  S4 = Toggle Switch [package=THT]
  R3 = Resistor [tolerance=±5% resistance=220 package=THT]
  BAT1 = Battery Holders [package=battery-aa-kit]
  BAT2 = Battery Holders [package=battery-aa-kit]
  BAT4 = Battery Holders [package=battery-aa-kit]
  BAT3 = Battery Holders [package=battery-aa-kit]

nets:
  GND: Εξάρτημα2.GND, Part1.GND, SD_card_module1.GND, LED2.cathode, M1.GND, R3.Pin_1, BAT1.-, BAT2.-, BAT4.-, BAT3.-
  N1: Εξάρτημα2.D3, M1.Tx
  N2: Εξάρτημα2.D4, M1.Rx
  N3: Εξάρτημα2.D5, S4.L2
  N4: Εξάρτημα2.D6, R2.Pin_1
  N5: Εξάρτημα2.D10, SD_card_module1.CS
  N6: Εξάρτημα2.D11/MOSI, SD_card_module1.MOSI
  N7: Εξάρτημα2.D12/MISO, SD_card_module1.MISO
  N8: Εξάρτημα2.VIN, S3.L2
  N9: Εξάρτημα2.5V, SD_card_module1.+5
  N10: Εξάρτημα2.A0, Part1.OUTPUT
  3V3: Εξάρτημα2.3V3, Part1.VDD
  N11: Εξάρτημα2.D13/SCK, SD_card_module1.SCK
  N12: LED2.anode, R2.Pin_0
  N13: S3.L1, BAT1.+, BAT2.+, BAT4.+, BAT3.+
  N14: S4.COM, R3.Pin_0

custom parts:
  Adafruit MAX9814 Electret Microphone Amplifier: Add an ear to your project with this well-designed electret microphone amplifier with AGC. This fully assembled and tested board comes with a 20-20KHz electret microphone soldered on. For the amplification, we use the Maxim MAX9814, a specialty chip that is designed for amplifying electret microphones in situations where the loudness of the audio isn't predictable. This fancy microphone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
  SD Card Module: SD Card Module Slot Socket Reader For Arduino ARM MCU
  NEO-6M GPS Module: GY-GPS6MV2 NEO-6M GPS Module Module based on U-blox NEO-6M GPS engine, incorporating regulator for 3.3-5V DC input, MS621FE-compatible rechargeable battery for backup and EEPROM for storing configuration settings. Links: NEO-6 series product information page NEO-6 Datasheet
